// Digital circuit P40.dig as structural Verilog
module P40 (
  input  [31:0] instr,
  output illegal
);

  wire and_1_out, and_2_out, and_3_out, and_4_out, and_5_out, and_6_out, and_7_out, and_8_out, and_9_out,
       and_10_out, and_11_out, and_12_out, and_13_out, comparator_1_eq, comparator_2_eq, comparator_3_eq,
       comparator_4_eq, comparator_5_eq, comparator_6_eq, comparator_7_eq, comparator_8_eq, comparator_9_eq,
       comparator_10_eq, comparator_11_eq, comparator_12_eq, comparator_13_eq, comparator_14_eq,
       comparator_15_eq, comparator_16_eq, comparator_17_eq, comparator_18_eq, comparator_19_eq,
       comparator_20_eq, comparator_21_eq, comparator_22_eq, not_1_out, not_2_out, not_3_out, or_1_out,
       or_2_out, or_3_out, or_4_out, or_5_out, or_6_out, or_7_out, or_8_out, or_9_out, or_10_out, or_11_out,
       or_12_out, or_13_out, or_14_out, or_15_out, or_16_out, or_17_out, or_18_out, or_19_out, or_20_out,
       or_21_out, or_22_out, or_23_out, or_24_out;

  Comparator #(.Bits(7)) comparator_1 (.a(instr[6:0]), .b(7'b0110111), .eq(comparator_1_eq));  // open: gt, lt
  Comparator #(.Bits(7)) comparator_2 (.a(instr[6:0]), .b(7'b0010111), .eq(comparator_2_eq));  // open: gt, lt
  Comparator #(.Bits(7)) comparator_3 (.a(instr[6:0]), .b(7'b1101111), .eq(comparator_3_eq));  // open: gt, lt
  Comparator #(.Bits(7)) comparator_4 (.a(instr[6:0]), .b(7'b1100111), .eq(comparator_4_eq));  // open: gt, lt
  Comparator #(.Bits(7)) comparator_5 (.a(instr[6:0]), .b(7'b1100011), .eq(comparator_5_eq));  // open: gt, lt
  Comparator #(.Bits(7)) comparator_6 (.a(instr[6:0]), .b(7'b0000011), .eq(comparator_6_eq));  // open: gt, lt
  Comparator #(.Bits(7)) comparator_7 (.a(instr[6:0]), .b(7'b0100011), .eq(comparator_7_eq));  // open: gt, lt
  Comparator #(.Bits(7)) comparator_8 (.a(instr[6:0]), .b(7'b0010011), .eq(comparator_8_eq));  // open: gt, lt
  Comparator #(.Bits(7)) comparator_9 (.a(instr[6:0]), .b(7'b0110011), .eq(comparator_9_eq));  // open: gt, lt
  Comparator #(.Bits(7)) comparator_10 (.a(instr[6:0]), .b(7'b1110011), .eq(comparator_10_eq));  // open: gt, lt
  Comparator #(.Bits(3)) comparator_11 (.a(instr[14:12]), .b(3'b000), .eq(comparator_11_eq));  // open: gt, lt
  Comparator #(.Bits(3)) comparator_12 (.a(instr[14:12]), .b(3'b001), .eq(comparator_12_eq));  // open: gt, lt
  Comparator #(.Bits(3)) comparator_13 (.a(instr[14:12]), .b(3'b010), .eq(comparator_13_eq));  // open: gt, lt
  Comparator #(.Bits(3)) comparator_14 (.a(instr[14:12]), .b(3'b011), .eq(comparator_14_eq));  // open: gt, lt
  Comparator #(.Bits(3)) comparator_15 (.a(instr[14:12]), .b(3'b100), .eq(comparator_15_eq));  // open: gt, lt
  Comparator #(.Bits(3)) comparator_16 (.a(instr[14:12]), .b(3'b101), .eq(comparator_16_eq));  // open: gt, lt
  Comparator #(.Bits(3)) comparator_17 (.a(instr[14:12]), .b(3'b110), .eq(comparator_17_eq));  // open: gt, lt
  Comparator #(.Bits(3)) comparator_18 (.a(instr[14:12]), .b(3'b111), .eq(comparator_18_eq));  // open: gt, lt
  Comparator #(.Bits(7)) comparator_19 (.a(instr[31:25]), .b({7{1'b0}}), .eq(comparator_19_eq));  // open: gt, lt
  Comparator #(.Bits(7)) comparator_20 (.a(instr[31:25]), .b(7'b0100000), .eq(comparator_20_eq));  // open: gt, lt
  Comparator #(.Bits(32)) comparator_21 (.a(instr), .b(32'h73), .eq(comparator_21_eq));  // open: gt, lt
  Comparator #(.Bits(32)) comparator_22 (.a(instr), .b(32'h30200073), .eq(comparator_22_eq));  // open: gt, lt
  and and_1 (and_1_out, comparator_4_eq, comparator_11_eq);
  or or_1 (or_1_out, comparator_13_eq, comparator_14_eq);
  or or_2 (or_2_out, comparator_11_eq, comparator_13_eq);
  or or_3 (or_3_out, comparator_11_eq, comparator_13_eq);
  and and_2 (and_2_out, comparator_12_eq, comparator_19_eq);
  and and_3 (and_3_out, comparator_16_eq, or_8_out);
  or or_4 (or_4_out, comparator_12_eq, comparator_16_eq);
  and and_4 (and_4_out, comparator_11_eq, or_8_out);
  and and_5 (and_5_out, comparator_16_eq, or_8_out);
  or or_5 (or_5_out, comparator_11_eq, comparator_16_eq);
  or or_6 (or_6_out, comparator_21_eq, comparator_22_eq);
  or or_7 (or_7_out, comparator_12_eq, comparator_13_eq);
  or or_8 (or_8_out, comparator_19_eq, comparator_20_eq);
  not not_1 (not_1_out, or_1_out);
  or or_9 (or_9_out, or_2_out, comparator_15_eq);
  and and_6 (and_6_out, comparator_7_eq, or_3_out);
  or or_10 (or_10_out, and_2_out, and_3_out);
  not not_2 (not_2_out, or_4_out);
  or or_11 (or_11_out, and_4_out, and_5_out);
  not not_3 (not_3_out, or_5_out);
  and and_7 (and_7_out, comparator_11_eq, or_6_out);
  or or_12 (or_12_out, or_7_out, comparator_14_eq);
  and and_8 (and_8_out, comparator_5_eq, not_1_out);
  and and_9 (and_9_out, comparator_6_eq, or_9_out);
  or or_13 (or_13_out, not_2_out, or_10_out);
  and and_10 (and_10_out, not_3_out, comparator_19_eq);
  or or_14 (or_14_out, and_7_out, or_12_out);
  and and_11 (and_11_out, comparator_8_eq, or_13_out);
  or or_15 (or_15_out, or_11_out, and_10_out);
  and and_12 (and_12_out, comparator_10_eq, or_14_out);
  not not_4 (illegal, or_24_out);
  and and_13 (and_13_out, comparator_9_eq, or_15_out);
  or or_16 (or_16_out, comparator_1_eq, comparator_2_eq);
  or or_17 (or_17_out, comparator_3_eq, and_1_out);
  or or_18 (or_18_out, and_8_out, and_9_out);
  or or_19 (or_19_out, and_6_out, and_11_out);
  or or_20 (or_20_out, and_13_out, and_12_out);
  or or_21 (or_21_out, or_16_out, or_17_out);
  or or_22 (or_22_out, or_18_out, or_19_out);
  or or_23 (or_23_out, or_21_out, or_22_out);
  or or_24 (or_24_out, or_23_out, or_20_out);

  // Notes on the sheet:
  //   P40 Illegal-instruction detector - Digital task
  //   Full size: decode opcode/funct3/funct7 with gates (Comparators with Consts allowed).
  //   Allowed parts: all of the above + Add, Sub, Comparator, Neg
  //   Do not rename, move or delete the input and output pins.
endmodule

/* Test case public tests:
instr illegal
1085628339 0
133588371 0
4120596342 1
1073750067 1
1048691 1
2032652061 1
12323 1
2721039909 1
20483 1
4277626595 0
1081497107 0
16217747 0
3825785736 1
1081497107 0
3212547 0
1081497107 0
1081497107 0
33554483 1
22686131 0
1081497107 0
115 0
4199 1
3267572968 1
133588371 0
32888211 0
1811891546 1
3212547 0
1616716053 1
872822259 0
1940214897 1
239 0
239 0
16499 1
4241906403 0
15132211 0
133588371 0
1085628339 0
1804168177 1
4887 0
1126311521 1
12944691 0
4278255891 0
11731875 0
16217747 0
18380723 0
1073750067 1
4280362531 0
32431667 0
67473542 1
25934643 0
11731875 0
1073745939 1
661752509 1
133588371 0
8291 1
25934643 0
127 1
20483 1
133588371 0
127 1
1972542262 1
1647611964 1
4277626595 0
16499 1
25934643 0
239 0
32431667 0
33554483 1
19 0
3355645119 1
25934643 0
4294198147 0
19174451 0
12323 1
3212547 0
19174451 0
15132211 0
4289929875 0
807403635 0
15132211 0
273678451 1
8291 1
3293765469 1
4280362531 0
872822259 0
12656771 0
4131 1
3830096170 1
12656771 0
33554483 1
19174451 0
844189251 1
16499 1
4099 1
807403635 0
12323 1
1085628339 0
4277626595 0
4294264083 0
4294198147 0
305419575 0
16499 1
807403635 0
1085628339 0
19 0
133588371 0
16217747 0
3478803 0
1888433689 1
32888211 0
4271131875 0
1667113086 1
0 1
1073745939 1
4099 1
2526064425 1
4294264083 0
4241906403 0
3429947459 1
115 0
18380723 0
807403635 0
4289929875 0
805315955 0
305419575 0
4277626595 0
32431667 0
5452435 0
4271131875 0
3034857512 1
33554483 1
3478803 0
127 1
1048691 1
2105360533 1
914139815 1
3280729903 1
4131 1
29183155 0
15132211 0
20483 1
2468019094 1
4241906403 0
4294264083 0
4261581539 0
4131 1
4099 1
12944691 0
4289929875 0
16217747 0
4099 1
1081497107 0
1081279155 0
3993073811 0
15 1
4099 1
1679565827 0
18380723 0
4131 1
32888211 0
*/
